# Fritzing sketch focosArduino (saved by Fritzing 0.9.3b)

parts:
  U1 = 4-Channel 5v Relay Shield [package=relay-4ch5v10a]
  FOCO2 = FOCO [package=led10mm]
  FOCO1 = FOCO [package=led10mm]
  FOCO4 = FOCO [package=led10mm]
  FOCO3 = FOCO [package=led10mm]
  Power_plug1 = Power plug
  Arduino2 = Arduino Uno (Rev3)

nets:
  VCC: U1.VCC, Arduino2.5V
  GND: U1.GND, Power_plug1.GND, Arduino2.GND
  N1: U1.IN1, Arduino2.A3
  N2: U1.IN2, Arduino2.A2
  N3: U1.K1-Off, U1.K2-Off, U1.K3-Off, U1.K4-Off
  N4: U1.K1-On, FOCO4.C
  N5: U1.K2-On, FOCO3.C
  N6: U1.IN4, Arduino2.A0
  N7: U1.K3-On, FOCO2.C
  N8: U1.K4-On, FOCO1.C
  N9: U1.IN3, Arduino2.A1
  N10: FOCO2.A, FOCO1.A, FOCO4.A, FOCO3.A

custom parts:
  4-Channel 5v Relay Shield: 4 Channel 5v Relay Shield w. 2x SPD-06VDC-SD-C
  FOCO: LEDs Standard schematic elements and footprints for 5mm, 3mm, 1206, and 0603 sized LEDs. 5mm - Spark Fun Electronics SKU : COM-00529 (and others)
