# Fritzing sketch focosPico (saved by Fritzing 0.9.3b)
breadboards: 1

parts:
  U1 = 4-Channel 5v Relay Shield [package=relay-4ch5v10a]
  FOCO2 = FOCO [package=led10mm]
  FOCO1 = FOCO [package=led10mm]
  FOCO4 = FOCO [package=led10mm]
  FOCO3 = FOCO [package=led10mm]
  Power_plug1 = Power plug  # not connected
  Mod2 = Raspberry Pi Pico

nets:
  N1: U1.VCC, Mod2.pin_36
  N2: U1.GND, Mod2.pin_3, Mod2.pin_8, Mod2.pin_13, Mod2.pin_18, Mod2.pin_23, Mod2.pin_28, Mod2.pin_33, Mod2.pin_38, Mod2.pin_42
  N3: U1.IN1, Mod2.pin_34
  N4: U1.IN2, Mod2.pin_32
  N5: U1.K1-Off, U1.K2-Off, U1.K3-Off, U1.K4-Off
  N6: U1.K1-On, FOCO4.C
  N7: U1.K2-On, FOCO3.C
  N8: U1.IN4, Mod2.pin_29
  N9: U1.K3-On, FOCO2.C
  N10: U1.K4-On, FOCO1.C
  N11: U1.IN3, Mod2.pin_31
  N12: FOCO2.A, FOCO1.A, FOCO4.A, FOCO3.A

custom parts:
  4-Channel 5v Relay Shield: 4 Channel 5v Relay Shield w. 2x SPD-06VDC-SD-C
  FOCO: LEDs Standard schematic elements and footprints for 5mm, 3mm, 1206, and 0603 sized LEDs. 5mm - Spark Fun Electronics SKU : COM-00529 (and others)
  Raspberry Pi Pico: Raspberry Pi Pico. Based around the RP2040 microcontroller the Pico is a low cost microcontroller device bringing Raspberry Pi quality, cost, and easy of use to the microcontroller space. Jan 2021, Split part in to two versions: tht (this one) and SMD. This one will drill holes for a .1 in header in pcb to allow plugging in the module as well as providing pads to solder the module to the top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
